// Logisim project ALU.circ as structural Verilog: 1 circuit, main circuit main
module main (
  input  [7:0] A,
  input  [7:0] B,
  input  Enabler,
  input  [3:0] Instruction,
  output [7:0] Output,
  output LZ,
  output LE,
  output EQ,
  output GE,
  output GZ
);

  wire clock_1_out, comparator_1_eq, comparator_1_gt, comparator_1_lt, or_1_out, or_2_out;
  wire [7:0] adder_1_out, multiplier_1_out, subtractor_1_out;

  Comparator comparator_1 (.a(A), .b({8{1'b0}}), .gt(comparator_1_gt), .eq(comparator_1_eq), .lt(comparator_1_lt));
  or or_1 (or_1_out, comparator_1_lt, comparator_1_eq);
  Register #(.width(1)) register_1 (.D(comparator_1_lt), .Q(LZ), .clk(clock_1_out));  // open: en, clr
  Adder adder_1 (.a(A), .b(B), .out(adder_1_out));  // open: cin, cout
  Subtractor subtractor_1 (.a(B), .b(A), .out(subtractor_1_out));  // open: bin, bout
  Multiplier multiplier_1 (.a(A), .b(B), .out(multiplier_1_out));  // open: cin, cout
  Register #(.width(1)) register_2 (.D(or_1_out), .Q(LE), .clk(clock_1_out));  // open: en, clr
  or or_2 (or_2_out, comparator_1_eq, comparator_1_gt);
  Register #(.width(1)) register_3 (.D(or_2_out), .Q(GE), .clk(clock_1_out));  // open: en, clr
  Register #(.width(1)) register_4 (.D(comparator_1_eq), .Q(EQ), .clk(clock_1_out));  // open: en, clr
  Register #(.width(1)) register_5 (.D(comparator_1_gt), .Q(GZ), .clk(clock_1_out));  // open: en, clr
  Clock clock_1 (.out(clock_1_out));
  Multiplexer #(.select(4), .width(8)) multiplexer_1 (
    .in0({8{1'b0}}), .in1({8{1'b0}}), .in2({8{1'b0}}), .in3({8{1'b0}}), .in4(adder_1_out),
    .in5(subtractor_1_out), .in6({8{1'b0}}), .in7(multiplier_1_out), .in8({8{1'b0}}), .in9({8{1'b0}}),
    .in10({8{1'b0}}), .in11({8{1'b0}}), .in12({8{1'b0}}), .in13({8{1'b0}}), .in14({8{1'b0}}),
    .in15({8{1'b0}}), .out(Output), .sel(Instruction), .en(Enabler));
endmodule
