// Logisim project Adder.circ as structural Verilog: 4 circuits, main circuit 8-bit Adder
module Full_Adder (
  input  Input__One_of_the_numbers_to_add,
  input  Input__One_of_the_numbers_to_add_2,
  input  Carry_In,
  output Sum,
  output Carry_Out
);

  wire and_1_out, and_2_out, and_3_out, and_4_out, and_5_out, not_1_out, xnor_1_out, xor_1_out;

  and and_1 (and_1_out, Input__One_of_the_numbers_to_add_2, Carry_In);
  and and_2 (and_2_out, Input__One_of_the_numbers_to_add, Carry_In);
  and and_3 (and_3_out, Input__One_of_the_numbers_to_add, Input__One_of_the_numbers_to_add_2);
  not not_1 (not_1_out, Input__One_of_the_numbers_to_add);
  xor xor_1 (xor_1_out, Input__One_of_the_numbers_to_add_2, Carry_In);
  xnor xnor_1 (xnor_1_out, Input__One_of_the_numbers_to_add_2, Carry_In);
  or or_1 (Carry_Out, and_1_out, and_2_out, and_3_out);
  and and_4 (and_4_out, not_1_out, xor_1_out);
  or or_2 (Sum, and_4_out, and_5_out);
  and and_5 (and_5_out, Input__One_of_the_numbers_to_add, xnor_1_out);
endmodule

module _2_bit_Adder (
  input  Carry_In,
  input  [1:0] Input__One_of_the_inputs_to_be_added,
  input  [1:0] Input__One_of_the_inputs_to_be_added_2,
  output [1:0] Sum,
  output Carry_Out
);

  wire full_adder_1_carry_out;

  Full_Adder full_adder_1 (
    .Input__One_of_the_numbers_to_add(Input__One_of_the_inputs_to_be_added_2[0]),
    .Input__One_of_the_numbers_to_add_2(Input__One_of_the_inputs_to_be_added[0]), .Carry_In(Carry_In),
    .Sum(Sum[0]), .Carry_Out(full_adder_1_carry_out));
  Full_Adder full_adder_2 (
    .Input__One_of_the_numbers_to_add(Input__One_of_the_inputs_to_be_added_2[1]),
    .Input__One_of_the_numbers_to_add_2(Input__One_of_the_inputs_to_be_added[1]),
    .Carry_In(full_adder_1_carry_out), .Sum(Sum[1]), .Carry_Out(Carry_Out));
endmodule

module _4_bit_Adder (
  input  Carry_In,
  input  [3:0] Input__One_of_the_inputs_to_be_added,
  input  [3:0] Input__One_of_the_inputs_to_be_added_2,
  output [3:0] Sum,
  output Carry_Out
);

  wire n2_bit_adder_1_carry_out;

  _2_bit_Adder u_2_bit_adder_1 (
    .Carry_In(Carry_In), .Input__One_of_the_inputs_to_be_added(Input__One_of_the_inputs_to_be_added_2[1:0]),
    .Input__One_of_the_inputs_to_be_added_2(Input__One_of_the_inputs_to_be_added[1:0]),
    .Carry_Out(n2_bit_adder_1_carry_out), .Sum(Sum[1:0]));
  _2_bit_Adder u_2_bit_adder_2 (
    .Carry_In(n2_bit_adder_1_carry_out),
    .Input__One_of_the_inputs_to_be_added(Input__One_of_the_inputs_to_be_added_2[3:2]),
    .Input__One_of_the_inputs_to_be_added_2(Input__One_of_the_inputs_to_be_added[3:2]),
    .Carry_Out(Carry_Out), .Sum(Sum[3:2]));
endmodule

module _8_bit_Adder (
  input  in_1,
  input  [7:0] Input__One_of_the_inputs_to_be_added,
  input  [7:0] Input__One_of_the_inputs_to_be_added_2,
  output [7:0] out_4,
  output Carry_Out
);

  wire n4_bit_adder_1_carry_out;

  _4_bit_Adder u_4_bit_adder_1 (
    .Sum(out_4[3:0]), .Carry_In(in_1),
    .Input__One_of_the_inputs_to_be_added(Input__One_of_the_inputs_to_be_added_2[3:0]),
    .Input__One_of_the_inputs_to_be_added_2(Input__One_of_the_inputs_to_be_added[3:0]),
    .Carry_Out(n4_bit_adder_1_carry_out));
  _4_bit_Adder u_4_bit_adder_2 (
    .Sum(out_4[7:4]), .Carry_In(n4_bit_adder_1_carry_out),
    .Input__One_of_the_inputs_to_be_added(Input__One_of_the_inputs_to_be_added_2[7:4]),
    .Input__One_of_the_inputs_to_be_added_2(Input__One_of_the_inputs_to_be_added[7:4]), .Carry_Out(Carry_Out));
endmodule
