// Logisim project Subtractor.circ as structural Verilog: 2 circuits, main circuit 8-bit Subtractor
module _8_bit_Subtractor (
  input  [7:0] in_1,
  input  [7:0] in_2,
  output [7:0] out_3,
  output out_4
);

  wire [7:0] not_1_out;

  _8_bit_Adder u_8_bit_adder_1 (
    .out_4(out_3), .in_1(1'b1), .Input__One_of_the_inputs_to_be_added(not_1_out),
    .Input__One_of_the_inputs_to_be_added_2(in_2), .Carry_Out(out_4));
  assign not_1_out = ~in_1;  // NOT_Gate not_1, 8 bits wide
endmodule

module _4_bit_Subtractor (
  input  [3:0] in_1,
  input  [3:0] in_2,
  output [3:0] out_3,
  output out_4
);

  wire [3:0] not_1_out;

  _4_bit_Adder u_4_bit_adder_1 (
    .Sum(out_3), .Carry_In(1'b1), .Input__One_of_the_inputs_to_be_added(in_2),
    .Input__One_of_the_inputs_to_be_added_2(not_1_out), .Carry_Out(out_4));
  assign not_1_out = ~in_1;  // NOT_Gate not_1, 4 bits wide
endmodule
