// Logisim project fetch.circ as structural Verilog: 1 circuit, main circuit main
// 32
module main (
  input  [7:0] PC_IN,
  output [7:0] OP_CODE,
  output [3:0] RA___FLAG,
  output [3:0] RB,
  output [7:0] CONST___NEW_PC,
  output ENABLE,
  output [7:0] PC_OUT
);

  wire clock_1_out, demultiplexer_1_out0, demultiplexer_1_out1;
  wire [1:0] bitselector_1_out;
  wire [7:0] adder_1_out, counter_1_q, register_2_q, rom_1_data;

  Clock clock_1 (.out(clock_1_out));
  Counter #(.max('h2)) counter_1 (.Q(counter_1_q), .clk(clock_1_out));  // open: load, D, count, carry, clr
  BitSelector #(.group(2)) bitselector_1 (.in(counter_1_q), .out(bitselector_1_out), .sel(2'b00));
  Adder adder_1 (.a(counter_1_q), .b(PC_IN), .out(adder_1_out));  // open: cin, cout
  Demultiplexer #(.select(2)) demultiplexer_1 (
    .out0(demultiplexer_1_out0), .out1(demultiplexer_1_out1), .out2(ENABLE), .in(1'b1),
    .sel(bitselector_1_out));  // open: out3, en
  ROM rom_1 (.addr(adder_1_out), .data(rom_1_data));  // open: sel
  Adder adder_2 (.a(8'h3), .b(PC_IN), .out(PC_OUT));  // open: cin, cout
  Register register_1 (.D(rom_1_data), .en(demultiplexer_1_out0), .Q(OP_CODE), .clk(clock_1_out));  // open: clr
  Register register_2 (.D(rom_1_data), .en(demultiplexer_1_out1), .Q(register_2_q), .clk(clock_1_out));  // open: clr
  Register register_3 (.D(rom_1_data), .en(ENABLE), .Q(CONST___NEW_PC), .clk(clock_1_out));  // open: clr
  BitSelector #(.group(4)) bitselector_2 (.in(register_2_q), .out(RA___FLAG), .sel(1'b0));
  BitSelector #(.group(4)) bitselector_3 (.in(register_2_q), .out(RB), .sel(1'b1));

  // Notes on the sheet:
  //   contents of rom_1 (hex, n*v repeats v):
  //   0 0 0 1 2 3
endmodule
