// Logisim project final.circ as structural Verilog: 6 circuits, main circuit main
// %ecx
module main (
  output [3:0] Instruction_Code,
  output [7:0] Output_Debug,
  output [2:0] Register_A,
  output [7:0] CONST,
  output [2:0] Register_B,
  output [7:0] Memory_Address_A,
  output [7:0] Memory_Address_B,
  output [7:0] Memory_Data_Debug
);

  wire comparator_1_out_8, decoder_1_out0, decoder_1_out1, decoder_1_out2, decoder_1_out3, decoder_1_out4,
       decoder_1_out5, decoder_1_out6, decoder_1_out7, decoder_1_out8, decoder_1_out15, fetch_1_enable,
       main_1_eq, main_1_ge, main_1_gz, main_1_le, main_1_lz, or_1_out, or_2_out, or_3_out;
  wire [2:0] multiplexer_2_out, multiplexer_7_out;
  wire [3:0] fetch_1_ra_flag, fetch_1_rb;
  wire [7:0] fetch_1_op_code, fetch_1_pc_out, main_1_output, memory_bus_1_read_data, multiplexer_1_out,
       multiplexer_3_out, multiplexer_4_out, multiplexer_5_out;

  fetch fetch_1 (
    .PC_IN(multiplexer_1_out), .HALT(decoder_1_out15), .OP_CODE(fetch_1_op_code), .RB(fetch_1_rb),
    .RA_FLAG(fetch_1_ra_flag), .CONST___NEW_PC(CONST), .ENABLE(fetch_1_enable), .PC_OUT(fetch_1_pc_out));
  Multiplexer #(.width(8), .enable("false")) multiplexer_1 (
    .in0(fetch_1_pc_out), .in1(CONST), .out(multiplexer_1_out), .sel(comparator_1_out_8));
  BitSelector #(.group(4)) bitselector_1 (.in(fetch_1_op_code), .out(Instruction_Code), .sel(1'b0));
  BitSelector #(.width(4), .group(3)) bitselector_2 (.in(fetch_1_rb), .out(Register_B), .sel(1'b0));
  BitSelector #(.width(4), .group(3)) bitselector_3 (.in(fetch_1_ra_flag), .out(Register_A), .sel(1'b0));
  Decoder #(.select(4)) decoder_1 (
    .out0(decoder_1_out0), .out1(decoder_1_out1), .out2(decoder_1_out2), .out3(decoder_1_out3),
    .out4(decoder_1_out4), .out5(decoder_1_out5), .out6(decoder_1_out6), .out7(decoder_1_out7),
    .out8(decoder_1_out8), .out15(decoder_1_out15), .sel(Instruction_Code), .en(fetch_1_enable));  // open: out9, out10, out11, out12, out13, out14
  Multiplexer #(.width(3), .enable("false")) multiplexer_2 (
    .in0(Register_B), .in1(Register_A), .out(multiplexer_2_out), .sel(decoder_1_out3));
  or or_1 (or_1_out, decoder_1_out1, decoder_1_out2, decoder_1_out3, decoder_1_out7, decoder_1_out4, decoder_1_out5);
  Multiplexer #(.width(8), .enable("false")) multiplexer_3 (
    .in0(Memory_Address_A), .in1(Memory_Address_B), .out(multiplexer_3_out), .sel(decoder_1_out0));
  Multiplexer #(.width(8), .enable("false")) multiplexer_4 (
    .in0(memory_bus_1_read_data), .in1(Memory_Address_A), .out(multiplexer_4_out), .sel(decoder_1_out2));
  or or_2 (or_2_out, decoder_1_out7, decoder_1_out4, decoder_1_out5);
  Multiplexer #(.width(8), .enable("false")) multiplexer_5 (
    .in0(multiplexer_4_out), .in1(main_1_output), .out(multiplexer_5_out), .sel(or_2_out));
  Multiplexer #(.width(8), .enable("false")) multiplexer_6 (
    .in0(multiplexer_5_out), .in1(CONST), .out(Output_Debug), .sel(decoder_1_out3));
  _8x32_RF u_8x32_rf_1 (
    .Write1(Output_Debug), .Register_1_2(multiplexer_2_out), .WE(or_1_out), .Read1(Memory_Address_A),
    .RE(or_3_out), .Register_1(Register_A), .Read2(Memory_Address_B), .Register_2(Register_B));  // open: Register_2_2, Write2
  memory_bus memory_bus_1 (
    .Address(multiplexer_3_out), .WE(decoder_1_out0), .RE(decoder_1_out1), .Write_Data(Memory_Address_A),
    .Read_Data(memory_bus_1_read_data));
  or or_3 (or_3_out, decoder_1_out7, decoder_1_out4, decoder_1_out2, decoder_1_out6, decoder_1_out0, decoder_1_out5, decoder_1_out1);
  ALU_main main_1 (
    .A(Memory_Address_A), .B(Memory_Address_B), .Instruction(Instruction_Code), .Output(main_1_output),
    .LZ(main_1_lz), .LE(main_1_le), .EQ(main_1_eq), .GE(main_1_ge), .GZ(main_1_gz), .Enabler(fetch_1_enable));
  Multiplexer #(.width(3), .enable("false")) multiplexer_7 (
    .in0(3'b111), .in1(Register_A), .out(multiplexer_7_out), .sel(decoder_1_out8));
  Comparator comparator_1 (
    .FLAG_VALUE(multiplexer_7_out), .AO(1'b1), .LZ(main_1_lz), .LE(main_1_le), .EQ(main_1_eq),
    .GE(main_1_ge), .GZ(main_1_gz), .out_8(comparator_1_out_8));

  assign Memory_Data_Debug = Memory_Address_A;
endmodule

module _8x32_RF (
  input  [7:0] Write1,
  input  RE,
  input  [2:0] Register_1,
  input  [2:0] Register_1_2,
  input  WE,
  input  [2:0] Register_2,
  input  [2:0] Register_2_2,
  input  [7:0] Write2,
  output [7:0] Read1,
  output [7:0] Read2
);

  wire clock_1_out, decoder_1_out0, decoder_1_out1, decoder_1_out2, decoder_1_out3, decoder_1_out4,
       decoder_1_out5, decoder_1_out6, decoder_1_out7, decoder_2_out0, decoder_2_out1, decoder_2_out2,
       decoder_2_out3, decoder_2_out4, decoder_2_out5, decoder_2_out6, decoder_2_out7, decoder_3_out0,
       decoder_3_out1, decoder_3_out2, decoder_3_out3, decoder_3_out4, decoder_3_out5, decoder_3_out6,
       decoder_3_out7, decoder_4_out0, decoder_4_out1, decoder_4_out2, decoder_4_out3, decoder_4_out4,
       decoder_4_out5, decoder_4_out6, decoder_4_out7, or_1_out, or_2_out, or_3_out, or_4_out, or_5_out,
       or_6_out, or_7_out, or_8_out;
  wire [7:0] multiplexer_1_out, multiplexer_2_out, multiplexer_3_out, multiplexer_4_out, multiplexer_5_out,
       multiplexer_6_out, multiplexer_7_out, multiplexer_8_out, ra_q, rb_q, rc_q, rd_q, re_q, rf_q, rg_q,
       rtmp_q;

  Decoder #(.select(3)) decoder_1 (
    .out0(decoder_1_out0), .out1(decoder_1_out1), .out2(decoder_1_out2), .out3(decoder_1_out3),
    .out4(decoder_1_out4), .out5(decoder_1_out5), .out6(decoder_1_out6), .out7(decoder_1_out7),
    .sel(Register_1_2), .en(WE));
  Decoder #(.select(3)) decoder_2 (
    .out0(decoder_2_out0), .out1(decoder_2_out1), .out2(decoder_2_out2), .out3(decoder_2_out3),
    .out4(decoder_2_out4), .out5(decoder_2_out5), .out6(decoder_2_out6), .out7(decoder_2_out7),
    .sel(Register_2_2), .en(WE));
  Multiplexer #(.width(8)) multiplexer_1 (
    .in0(Write2), .in1(Write1), .out(multiplexer_1_out), .sel(decoder_1_out0));  // open: en
  Multiplexer #(.width(8)) multiplexer_2 (
    .in0(Write2), .in1(Write1), .out(multiplexer_2_out), .sel(decoder_1_out1));  // open: en
  Multiplexer #(.width(8)) multiplexer_3 (
    .in0(Write2), .in1(Write1), .out(multiplexer_3_out), .sel(decoder_1_out2));  // open: en
  Multiplexer #(.width(8)) multiplexer_4 (
    .in0(Write2), .in1(Write1), .out(multiplexer_4_out), .sel(decoder_1_out3));  // open: en
  Multiplexer #(.width(8)) multiplexer_5 (
    .in0(Write2), .in1(Write1), .out(multiplexer_5_out), .sel(decoder_1_out4));  // open: en
  Multiplexer #(.width(8)) multiplexer_6 (
    .in0(Write2), .in1(Write1), .out(multiplexer_6_out), .sel(decoder_1_out5));  // open: en
  Multiplexer #(.width(8)) multiplexer_7 (
    .in0(Write2), .in1(Write1), .out(multiplexer_7_out), .sel(decoder_1_out6));  // open: en
  Multiplexer #(.width(8)) multiplexer_8 (
    .in0(Write2), .in1(Write1), .out(multiplexer_8_out), .sel(decoder_1_out7));  // open: en
  or or_1 (or_1_out, decoder_1_out0, decoder_2_out0);
  or or_2 (or_2_out, decoder_1_out1, decoder_2_out1);
  or or_3 (or_3_out, decoder_1_out2, decoder_2_out2);
  or or_4 (or_4_out, decoder_1_out3, decoder_2_out3);
  or or_5 (or_5_out, decoder_1_out4, decoder_2_out4);
  or or_6 (or_6_out, decoder_1_out5, decoder_2_out5);
  or or_7 (or_7_out, decoder_1_out6, decoder_2_out6);
  or or_8 (or_8_out, decoder_1_out7, decoder_2_out7);
  Clock clock_1 (.out(clock_1_out));
  Register rtmp (.D(multiplexer_1_out), .en(or_1_out), .Q(rtmp_q), .clk(clock_1_out));  // open: clr
  Register ra (.D(multiplexer_2_out), .en(or_2_out), .Q(ra_q), .clk(clock_1_out));  // open: clr
  Register rb (.D(multiplexer_3_out), .en(or_3_out), .Q(rb_q), .clk(clock_1_out));  // open: clr
  Register rc (.D(multiplexer_4_out), .en(or_4_out), .Q(rc_q), .clk(clock_1_out));  // open: clr
  Register rd (.D(multiplexer_5_out), .en(or_5_out), .Q(rd_q), .clk(clock_1_out));  // open: clr
  Register u_re (.D(multiplexer_6_out), .en(or_6_out), .Q(re_q), .clk(clock_1_out));  // open: clr
  Register rf (.D(multiplexer_7_out), .en(or_7_out), .Q(rf_q), .clk(clock_1_out));  // open: clr
  Register rg (.D(multiplexer_8_out), .en(or_8_out), .Q(rg_q), .clk(clock_1_out));  // open: clr
  assign Read1 = decoder_3_out0 ? rtmp_q : 8'bz;  // Controlled_Buffer controlled_buffer_1
  assign Read1 = decoder_3_out1 ? ra_q : 8'bz;  // Controlled_Buffer controlled_buffer_2
  assign Read1 = decoder_3_out2 ? rb_q : 8'bz;  // Controlled_Buffer controlled_buffer_3
  assign Read1 = decoder_3_out3 ? rc_q : 8'bz;  // Controlled_Buffer controlled_buffer_4
  assign Read1 = decoder_3_out4 ? rd_q : 8'bz;  // Controlled_Buffer controlled_buffer_5
  assign Read1 = decoder_3_out5 ? re_q : 8'bz;  // Controlled_Buffer controlled_buffer_6
  assign Read1 = decoder_3_out6 ? rf_q : 8'bz;  // Controlled_Buffer controlled_buffer_7
  assign Read1 = decoder_3_out7 ? rg_q : 8'bz;  // Controlled_Buffer controlled_buffer_8
  assign Read2 = decoder_4_out0 ? rtmp_q : 8'bz;  // Controlled_Buffer controlled_buffer_9
  assign Read2 = decoder_4_out1 ? ra_q : 8'bz;  // Controlled_Buffer controlled_buffer_10
  assign Read2 = decoder_4_out2 ? rb_q : 8'bz;  // Controlled_Buffer controlled_buffer_11
  assign Read2 = decoder_4_out3 ? rc_q : 8'bz;  // Controlled_Buffer controlled_buffer_12
  assign Read2 = decoder_4_out4 ? rd_q : 8'bz;  // Controlled_Buffer controlled_buffer_13
  assign Read2 = decoder_4_out5 ? re_q : 8'bz;  // Controlled_Buffer controlled_buffer_14
  assign Read2 = decoder_4_out6 ? rf_q : 8'bz;  // Controlled_Buffer controlled_buffer_15
  assign Read2 = decoder_4_out7 ? rg_q : 8'bz;  // Controlled_Buffer controlled_buffer_16
  Decoder #(.select(3)) decoder_3 (
    .out0(decoder_3_out0), .out1(decoder_3_out1), .out2(decoder_3_out2), .out3(decoder_3_out3),
    .out4(decoder_3_out4), .out5(decoder_3_out5), .out6(decoder_3_out6), .out7(decoder_3_out7),
    .sel(Register_1), .en(RE));
  Decoder #(.select(3)) decoder_4 (
    .out0(decoder_4_out0), .out1(decoder_4_out1), .out2(decoder_4_out2), .out3(decoder_4_out3),
    .out4(decoder_4_out4), .out5(decoder_4_out5), .out6(decoder_4_out6), .out7(decoder_4_out7),
    .sel(Register_2), .en(RE));
endmodule

module memory_bus (
  input  [7:0] Address,
  input  [7:0] Write_Data,
  input  WE,
  input  RE,
  output [7:0] Read_Data
);

  wire clock_1_out, not_1_out;
  wire [7:0] ram_1_data;

  Clock clock_1 (.out(clock_1_out));
  RAM ram_1 (.addr(Address), .data(ram_1_data), .clk(clock_1_out), .ld(not_1_out));  // open: sel, clr
  not not_1 (not_1_out, WE);
  assign ram_1_data = WE ? Read_Data : 8'bz;  // Controlled_Buffer controlled_buffer_1
  assign Read_Data = RE ? ram_1_data : 8'bz;  // Controlled_Buffer controlled_buffer_2
  assign Read_Data = WE ? Write_Data : 8'bz;  // Controlled_Buffer controlled_buffer_3
endmodule

module fetch (
  input  [7:0] PC_IN,
  input  HALT,
  output [7:0] OP_CODE,
  output [3:0] RB,
  output [3:0] RA_FLAG,
  output [7:0] CONST___NEW_PC,
  output ENABLE,
  output [7:0] PC_OUT
);

  wire clock_1_out, controlled_buffer_1_out, d_ff_1_q, demultiplexer_1_out0, demultiplexer_1_out1,
       demultiplexer_1_out2, not_1_out;
  wire [1:0] bitselector_1_out;
  wire [7:0] adder_1_out, counter_1_q, multiplexer_1_out, register_1_q, register_3_q, rom_1_data;

  Counter #(.max('h3)) counter_1 (.Q(counter_1_q), .clk(controlled_buffer_1_out));  // open: load, D, count, carry, clr
  Register register_1 (.D(PC_IN), .Q(register_1_q), .clk(controlled_buffer_1_out));  // open: en, clr
  assign controlled_buffer_1_out = not_1_out ? clock_1_out : 1'bz;  // Controlled_Buffer controlled_buffer_1
  not not_1 (not_1_out, d_ff_1_q);
  Clock clock_1 (.out(clock_1_out));
  BitSelector #(.group(2)) bitselector_1 (.in(counter_1_q), .out(bitselector_1_out), .sel(2'b00));
  Adder adder_1 (.a(counter_1_q), .b(register_1_q), .out(adder_1_out));  // open: cin, cout
  Multiplexer #(.width(8), .enable("false")) multiplexer_1 (
    .in0(adder_1_out), .in1(register_1_q), .out(multiplexer_1_out), .sel(d_ff_1_q));
  D_Flip_Flop d_ff_1 (.clk(d_ff_1_q), .Q(d_ff_1_q), .preset(HALT));  // open: D, Qn, en, reset
  Demultiplexer #(.select(2)) demultiplexer_1 (
    .out0(demultiplexer_1_out0), .out1(demultiplexer_1_out1), .out2(demultiplexer_1_out2), .out3(ENABLE),
    .in(1'b1), .sel(bitselector_1_out));  // open: en
  ROM rom_1 (.addr(multiplexer_1_out), .data(rom_1_data));  // open: sel
  Adder adder_2 (.a(8'h3), .b(register_1_q), .out(PC_OUT));  // open: cin, cout
  Register register_2 (
    .D(rom_1_data), .en(demultiplexer_1_out0), .Q(OP_CODE), .clk(controlled_buffer_1_out));  // open: clr
  BitSelector #(.group(4)) bitselector_2 (.in(register_3_q), .out(RB), .sel(1'b0));
  Register register_3 (
    .D(rom_1_data), .en(demultiplexer_1_out1), .Q(register_3_q), .clk(controlled_buffer_1_out));  // open: clr
  BitSelector #(.group(4)) bitselector_3 (.in(register_3_q), .out(RA_FLAG), .sel(1'b1));
  Register register_4 (
    .D(rom_1_data), .en(demultiplexer_1_out2), .Q(CONST___NEW_PC), .clk(controlled_buffer_1_out));  // open: clr

  // Notes on the sheet:
  //   contents of rom_1 (hex, n*v repeats v):
  //   3 0 1 2 1 0 3 0 0 0 10 0 3 0 3 2 1 0 3 0 1 0 10 0 3 0 5 2 1 0 3 0 2 0 10 0 3 0 5 2 1 0 3 0 3 0 10 0
  //   3 0 1 2 1 0 3 0 4 0 10 0 3 0 3 2 1 0 3 0 5 0 10 0 3 0 2 2 1 0 3 0 6 0 10 0 3 0 4 2 1 0 3 0 7 0 10 0
  //   3 0 0 1 1 0 3 0 4 1 2 0 3 0 1 1 3 0 3 0 6 1 4 0 7 12 0 7 34 0 4 24 0 3 0 8 0 40 0 3 0 0 1 1 0 3 0 5
  //   1 2 0 3 0 1 1 3 0 3 0 7 1 4 0 7 12 0 7 34 0 4 24 0 3 0 9 0 40 0 3 0 2 1 1 0 3 0 4 1 2 0 3 0 3 1 3 0
  //   3 0 6 1 4 0 7 12 0 7 34 0 4 24 0 3 0 a 0 40 0 3 0 2 1 1 0 3 0 5 1 2 0 3 0 3 1 3 0 3 0 7 1 4 0 7 12 0
  //   7 34 0 4 24 0 3 0 b 0 40 0 f
endmodule

module ALU (
  input  [7:0] A,
  input  [7:0] B,
  input  in_3,
  input  [3:0] Instruction,
  output [7:0] Output,
  output GE,
  output GZ,
  output LZ,
  output LE,
  output EQ
);

  wire clock_1_out, comparator_1_eq, comparator_1_gt, comparator_1_lt, or_1_out, or_2_out;
  wire [7:0] adder_1_out, multiplier_1_out, subtractor_1_out;

  Comparator_part comparator_1 (.a(A), .b({8{1'b0}}), .gt(comparator_1_gt), .eq(comparator_1_eq), .lt(comparator_1_lt));
  or or_1 (or_1_out, comparator_1_lt, comparator_1_eq);
  Register #(.width(1)) register_1 (.D(comparator_1_lt), .Q(LZ), .clk(clock_1_out));  // open: en, clr
  Adder adder_1 (.a(A), .b(B), .out(adder_1_out));  // open: cin, cout
  Subtractor subtractor_1 (.a(A), .b(B), .out(subtractor_1_out));  // open: bin, bout
  Multiplier multiplier_1 (.a(A), .b(B), .out(multiplier_1_out));  // open: cin, cout
  Register #(.width(1)) register_2 (.D(or_1_out), .Q(LE), .clk(clock_1_out));  // open: en, clr
  or or_2 (or_2_out, comparator_1_eq, comparator_1_gt);
  Register #(.width(1)) register_3 (.D(or_2_out), .Q(GE), .clk(clock_1_out));  // open: en, clr
  Register #(.width(1)) register_4 (.D(comparator_1_eq), .Q(EQ), .clk(clock_1_out));  // open: en, clr
  Register #(.width(1)) register_5 (.D(comparator_1_gt), .Q(GZ), .clk(clock_1_out));  // open: en, clr
  Multiplexer #(.select(4), .width(8)) multiplexer_1 (
    .in0({8{1'b0}}), .in1({8{1'b0}}), .in2({8{1'b0}}), .in3({8{1'b0}}), .in4(adder_1_out),
    .in5(subtractor_1_out), .in6({8{1'b0}}), .in7(multiplier_1_out), .in8({8{1'b0}}), .in9({8{1'b0}}),
    .in10({8{1'b0}}), .in11({8{1'b0}}), .in12({8{1'b0}}), .in13({8{1'b0}}), .in14({8{1'b0}}),
    .in15({8{1'b0}}), .out(Output), .sel(Instruction), .en(in_3));
  Clock clock_1 (.out(clock_1_out));
endmodule

module Comparator (
  input  [2:0] FLAG_VALUE,
  input  LE,
  input  EQ,
  input  GE,
  input  GZ,
  input  AO,
  input  LZ,
  output out_8
);

  wire and_1_out, and_2_out, and_3_out, and_4_out, and_5_out, and_6_out, decoder_1_out0, decoder_1_out1,
       decoder_1_out2, decoder_1_out3, decoder_1_out4, decoder_1_out5;

  Decoder #(.select(3), .enable("false")) decoder_1 (
    .out0(decoder_1_out0), .out1(decoder_1_out1), .out2(decoder_1_out2), .out3(decoder_1_out3),
    .out4(decoder_1_out4), .out5(decoder_1_out5), .sel(FLAG_VALUE));  // open: out6, out7
  and and_1 (and_1_out, decoder_1_out1, LZ);
  and and_2 (and_2_out, decoder_1_out0, AO);
  and and_3 (and_3_out, decoder_1_out3, EQ);
  and and_4 (and_4_out, decoder_1_out2, LE);
  or or_1 (out_8, and_2_out, and_1_out, and_4_out, and_3_out, and_5_out, and_6_out);
  and and_5 (and_5_out, decoder_1_out4, GE);
  and and_6 (and_6_out, decoder_1_out5, GZ);
endmodule
